# Fritzing sketch debouncing_due (saved by Fritzing 0.9.9b)
breadboards: 1

parts:
  Componente1 = Arduino Due (Rev2b)
  S1 = Pushbutton [package="[THT]"]
  C1 = Electrolytic Capacitor [capacitance=1µF voltage=35V package="100 mil [THT, electrolytic]"]
  R1 = Resistor [tolerance=±5% power=0.25 resistance=220 package=THT]
  S2 = Pushbutton [package="[THT]"]
  C2 = Electrolytic Capacitor [capacitance=1µF voltage=35V package="100 mil [THT, electrolytic]"]
  R2 = Resistor [tolerance=±5% power=0.25 resistance=220 package=THT]
  LED1 = LED - 5mm [color="Green (565nm)" current=0.030 package="5 mm [THT]"]
  R3 = Resistor [tolerance=±5% power=0.25 resistance=220 package=THT]
  LED2 = LED - 5mm [color="Green (565nm)" current=0.030 package="5 mm [THT]"]
  R4 = Resistor [tolerance=±5% power=0.25 resistance=220 package=THT]

nets:
  N1: Componente1.D14/TX3, S1.Pin_1, S1.Pin_2, C1.-, R1.Pin_0
  N2: Componente1.D16/TX2, LED2.cathode
  N3: Componente1.D17/RX2, S2.Pin_1, S2.Pin_2, C2.-, R2.Pin_0
  N4: Componente1.IOREF, Componente1.GND, R1.Pin_1, R2.Pin_1, R3.Pin_1, R4.Pin_1
  N5: Componente1.D40, LED1.cathode
  N6: S1.Pin_3, S1.Pin_4, C1.+, S2.Pin_3, S2.Pin_4, C2.+
  N7: LED1.anode, R3.Pin_0
  N8: LED2.anode, R4.Pin_0
