# Fritzing sketch debouncing_protoboard (saved by Fritzing 0.9.9b)
breadboards: 1

parts:
  S1 = Pushbutton [package="[THT]"]
  R1 = Resistor [tolerance=±5% power=0.25 resistance=220 package=THT]
  S2 = Pushbutton [package="[THT]"]
  R2 = Resistor [tolerance=±5% power=0.25 resistance=220 package=THT]
  LED1 = LED - 5mm [color="Green (565nm)" current=0.030 package="5 mm [THT]"]
  R3 = Resistor [tolerance=±5% power=0.25 resistance=220 package=THT]
  LED2 = LED - 5mm [color="Green (565nm)" current=0.030 package="5 mm [THT]"]
  R4 = Resistor [tolerance=±5% power=0.25 resistance=220 package=THT]
  C2 = Electrolytic Capacitor [capacitance=1µF voltage=35V package="100 mil [THT, electrolytic]"]
  C1 = Electrolytic Capacitor [capacitance=1µF voltage=35V package="100 mil [THT, electrolytic]"]

nets:
  N1: S1.Pin_1, S1.Pin_2, R1.Pin_0, C1.-
  N2: S1.Pin_3, S1.Pin_4, S2.Pin_3, S2.Pin_4, C2.+, C1.+
  N3: R1.Pin_1, R2.Pin_1, R3.Pin_1, R4.Pin_1
  N4: S2.Pin_1, S2.Pin_2, R2.Pin_0, C2.-
  N5: LED1.anode, R3.Pin_0
  N6: LED2.anode, R4.Pin_0
